# Fritzing sketch Untitled Sketch 2 (saved by Fritzing 1.0.5)
breadboards: 1

parts:
  Mod1 = Amica NodeMCU DEVKIT 1.0
  R1 = Resistor [tolerance=±5% resistance=220 package="0805 [SMD]"]
  LED1 = LED - 5mm [color="Red (633nm)" current=0.030A package="5 mm [THT]"]

nets:
  N1: Mod1.pin2, Mod1.pin_9, LED1.cathode
  N2: Mod1.pin8, R1.Pin_0
  N3: R1.Pin_1, LED1.anode
